# Fritzing sketch weather_station_schem (saved by Fritzing 0.9.10b)
breadboards: 1

parts:
  MCU = Heltec WiFi LoRa 32 V3 [part_number=HTIT-WB32LA]
  S2 = Pushbutton [package=THT]
  R1 = Resistor [tolerance=±5% power=0.25 resistance=10k package=THT]
  Wind_Speed = RJ9 [package=rj9]  # not connected
  Wind_Heading = RJ9 [package=rj9]  # not connected
  Rainfall = RJ9 [package=rj9]  # not connected

nets:
  N1: MCU.pin_16, MCU.pin_17
  N2: MCU.pin_18, MCU.pin_19
  N3: MCU.pin_21, MCU.pin_22
  N4: MCU.pin_26, R1.Pin_0
  N5: S2.leg0, R1.Pin_1
  GND: S2.leg1

custom parts:
  Heltec WiFi LoRa 32 V3: The Heltec WiFi LoRa 32 is an IoT development board designed and produced by Heltec Automation and based on the Espressif ESP32-S3FN8 and Semtech SX1262 modules. The board includes WiFi, Bluetooth and LoRa functions, as well as a 0.96″ OLED display and a lithium battery management system. Links: Heltec WiFi LoRa 32 product page Github
